// Logisim project Project#4.circ as structural Verilog: 1 circuit, main circuit main
module main (
);

  wire clock_1_out, clock_2_out, HB, HC, HD, HE, HF, MA, MB, MC, MD, ME, MF, n6to14_1_a1, n6to14_1_a_2,
       n6to14_1_b1, n6to14_1_b_2, n6to14_1_c1, n6to14_1_c_2, n6to14_1_d1, n6to14_1_d_2, n6to14_1_e1,
       n6to14_1_e_2, n6to14_1_f1, n6to14_1_f_2, n6to14_1_g, n6to14_1_g1, n6to14_2_a1, n6to14_2_a_2,
       n6to14_2_b1, n6to14_2_b_2, n6to14_2_c1, n6to14_2_c_2, n6to14_2_d1, n6to14_2_d_2, n6to14_2_e1,
       n6to14_2_e_2, n6to14_2_f1, n6to14_2_f_2, n6to14_2_g, n6to14_2_g1, n6to14_3_a1, n6to14_3_a_2,
       n6to14_3_b1, n6to14_3_b_2, n6to14_3_c1, n6to14_3_c_2, n6to14_3_d1, n6to14_3_d_2, n6to14_3_e1,
       n6to14_3_e_2, n6to14_3_f1, n6to14_3_f_2, n6to14_3_g, n6to14_3_g1, SA, SB, SC, SD, SE, SF;

  _7_Segment_Display u_7_segment_display_1 (
    .g(n6to14_1_g1), .f(n6to14_1_f1), .a(n6to14_1_a1), .b(n6to14_1_b1), .e(n6to14_1_e1), .d(n6to14_1_d1),
    .c(n6to14_1_c1));  // open: dp
  _6to14 u_6to14_1 (
    .A(HF), .B(HE), .C(HD), .D(HC), .E(HB), .F(1'b0), .A1(n6to14_1_a1), .F1(n6to14_1_f1), .B1(n6to14_1_b1),
    .G1(n6to14_1_g1), .E1(n6to14_1_e1), .D1(n6to14_1_d1), .C1(n6to14_1_c1), .A_2(n6to14_1_a_2),
    .F_2(n6to14_1_f_2), .B_2(n6to14_1_b_2), .G(n6to14_1_g), .E_2(n6to14_1_e_2), .D_2(n6to14_1_d_2),
    .C_2(n6to14_1_c_2));
  _7_Segment_Display u_7_segment_display_2 (
    .g(n6to14_1_g), .f(n6to14_1_f_2), .a(n6to14_1_a_2), .b(n6to14_1_b_2), .e(n6to14_1_e_2), .d(n6to14_1_d_2),
    .c(n6to14_1_c_2));  // open: dp
  Time_main main_1 (
    .SA(SA), .SB(SB), .SC(SC), .SD(SD), .SE(SE), .SF(SF), .MA(MA), .MB(MB), .MC(MC), .MD(MD), .ME(ME),
    .MF(MF), .HB(HB), .HC(HC), .HD(HD), .HE(HE), .HF(HF));
  Clock clock_1 (.out(clock_1_out));
  LED led_1 (.in(clock_1_out));
  LED led_2 (.in(clock_1_out));
  _6to14 u_6to14_2 (
    .A(MF), .B(ME), .C(MD), .D(MC), .E(MB), .F(MA), .A1(n6to14_2_a1), .F1(n6to14_2_f1), .B1(n6to14_2_b1),
    .G1(n6to14_2_g1), .E1(n6to14_2_e1), .D1(n6to14_2_d1), .C1(n6to14_2_c1), .A_2(n6to14_2_a_2),
    .F_2(n6to14_2_f_2), .B_2(n6to14_2_b_2), .G(n6to14_2_g), .E_2(n6to14_2_e_2), .D_2(n6to14_2_d_2),
    .C_2(n6to14_2_c_2));
  _7_Segment_Display u_7_segment_display_3 (
    .g(n6to14_2_g1), .f(n6to14_2_f1), .a(n6to14_2_a1), .b(n6to14_2_b1), .e(n6to14_2_e1), .d(n6to14_2_d1),
    .c(n6to14_2_c1));  // open: dp
  _7_Segment_Display u_7_segment_display_4 (
    .g(n6to14_2_g), .f(n6to14_2_f_2), .a(n6to14_2_a_2), .b(n6to14_2_b_2), .e(n6to14_2_e_2), .d(n6to14_2_d_2),
    .c(n6to14_2_c_2));  // open: dp
  Clock clock_2 (.out(clock_2_out));
  LED led_3 (.in(clock_2_out));
  LED led_4 (.in(clock_2_out));
  _7_Segment_Display u_7_segment_display_5 (
    .g(n6to14_3_g1), .f(n6to14_3_f1), .a(n6to14_3_a1), .b(n6to14_3_b1), .e(n6to14_3_e1), .d(n6to14_3_d1),
    .c(n6to14_3_c1));  // open: dp
  _6to14 u_6to14_3 (
    .A(SF), .B(SE), .C(SD), .D(SC), .E(SB), .F(SA), .A1(n6to14_3_a1), .F1(n6to14_3_f1), .B1(n6to14_3_b1),
    .G1(n6to14_3_g1), .E1(n6to14_3_e1), .D1(n6to14_3_d1), .C1(n6to14_3_c1), .A_2(n6to14_3_a_2),
    .F_2(n6to14_3_f_2), .B_2(n6to14_3_b_2), .G(n6to14_3_g), .E_2(n6to14_3_e_2), .D_2(n6to14_3_d_2),
    .C_2(n6to14_3_c_2));
  _7_Segment_Display u_7_segment_display_6 (
    .g(n6to14_3_g), .f(n6to14_3_f_2), .a(n6to14_3_a_2), .b(n6to14_3_b_2), .e(n6to14_3_e_2), .d(n6to14_3_d_2),
    .c(n6to14_3_c_2));  // open: dp

  // Notes on the sheet:
  //   Hours
  //   Minutes
  //   Seconds
endmodule
