// Logisim project Time.circ as structural Verilog: 1 circuit, main circuit main
module main (
  output SA,
  output SB,
  output SC,
  output SD,
  output SE,
  output SF,
  output MA,
  output MB,
  output MC,
  output MD,
  output ME,
  output MF,
  output HB,
  output HC,
  output HD,
  output HE,
  output HF
);

  wire and_1_out, and_2_out, and_3_out, clock_1_out, d_ff_1_qn, d_ff_2_qn, d_ff_3_qn, d_ff_4_qn, d_ff_5_qn,
       d_ff_6_qn, d_ff_7_qn, d_ff_8_qn, d_ff_9_qn, d_ff_10_qn, d_ff_11_qn, d_ff_12_qn, d_ff_13_qn,
       d_ff_14_qn, d_ff_15_qn, d_ff_16_qn;

  Clock clock_1 (.out(clock_1_out));
  not not_1 (SF, clock_1_out);
  D_Flip_Flop d_ff_1 (.clk(clock_1_out), .D(d_ff_1_qn), .Q(SE), .Qn(d_ff_1_qn), .reset(and_1_out));  // open: preset, en
  D_Flip_Flop d_ff_2 (.clk(d_ff_1_qn), .D(d_ff_2_qn), .Q(SD), .Qn(d_ff_2_qn), .reset(and_1_out));  // open: preset, en
  LED led_1 (.in(SA));
  LED led_2 (.in(SC));
  LED led_3 (.in(SB));
  D_Flip_Flop d_ff_3 (.clk(d_ff_2_qn), .D(d_ff_3_qn), .Q(SC), .Qn(d_ff_3_qn), .reset(and_1_out));  // open: preset, en
  LED led_4 (.in(SF));
  LED led_5 (.in(SE));
  LED led_6 (.in(SD));
  D_Flip_Flop d_ff_4 (.clk(d_ff_3_qn), .D(d_ff_4_qn), .Q(SB), .Qn(d_ff_4_qn), .reset(and_1_out));  // open: preset, en
  D_Flip_Flop d_ff_5 (.clk(d_ff_4_qn), .D(d_ff_5_qn), .Q(SA), .Qn(d_ff_5_qn), .reset(and_1_out));  // open: preset, en
  and and_1 (and_1_out, SA, SB, SC, SD);
  D_Flip_Flop d_ff_6 (.clk(and_1_out), .D(d_ff_6_qn), .Q(MF), .Qn(d_ff_6_qn), .reset(and_2_out));  // open: preset, en
  D_Flip_Flop d_ff_7 (.clk(d_ff_6_qn), .D(d_ff_7_qn), .Q(ME), .Qn(d_ff_7_qn), .reset(and_2_out));  // open: preset, en
  LED led_7 (.in(MA));
  LED led_8 (.in(MB));
  LED led_9 (.in(MC));
  D_Flip_Flop d_ff_8 (.clk(d_ff_7_qn), .D(d_ff_8_qn), .Q(MD), .Qn(d_ff_8_qn), .reset(and_2_out));  // open: preset, en
  LED led_10 (.in(MD));
  LED led_11 (.in(ME));
  D_Flip_Flop d_ff_9 (.clk(d_ff_8_qn), .D(d_ff_9_qn), .Q(MC), .Qn(d_ff_9_qn), .reset(and_2_out));  // open: preset, en
  LED led_12 (.in(MF));
  D_Flip_Flop d_ff_10 (
    .clk(d_ff_9_qn), .D(d_ff_10_qn), .Q(MB), .Qn(d_ff_10_qn), .reset(and_2_out));  // open: preset, en
  D_Flip_Flop d_ff_11 (
    .clk(d_ff_10_qn), .D(d_ff_11_qn), .Q(MA), .Qn(d_ff_11_qn), .reset(and_2_out));  // open: preset, en
  and and_2 (and_2_out, MD, MA, MB, MC);
  D_Flip_Flop d_ff_12 (
    .clk(and_2_out), .D(d_ff_12_qn), .Q(HF), .Qn(d_ff_12_qn), .reset(and_3_out));  // open: preset, en
  D_Flip_Flop d_ff_13 (
    .clk(d_ff_12_qn), .D(d_ff_13_qn), .Q(HE), .Qn(d_ff_13_qn), .reset(and_3_out));  // open: preset, en
  LED led_13 (.in(HB));
  D_Flip_Flop d_ff_14 (
    .clk(d_ff_13_qn), .D(d_ff_14_qn), .Q(HD), .Qn(d_ff_14_qn), .reset(and_3_out));  // open: preset, en
  LED led_14 (.in(HD));
  LED led_15 (.in(HC));
  LED led_16 (.in(HE));
  D_Flip_Flop d_ff_15 (
    .clk(d_ff_14_qn), .D(d_ff_15_qn), .Q(HC), .Qn(d_ff_15_qn), .reset(and_3_out));  // open: preset, en
  LED led_17 (.in(HF));
  D_Flip_Flop d_ff_16 (
    .clk(d_ff_15_qn), .D(d_ff_16_qn), .Q(HB), .Qn(d_ff_16_qn), .reset(and_3_out));  // open: preset, en
  and and_3 (and_3_out, HB, HC);
endmodule
